// Logisim project alu.circ as structural Verilog: 1 circuit, main circuit alu
module alu (
  input  [31:0] A,
  input  [31:0] B,
  input  [3:0] ALUSel,
  output [31:0] ALUResult
);

  wire comparator_1_lt;
  wire [31:0] add0, x0, x1, x2, x3, x4, x5, x6, x7, x8, x9, x10, x11, x12, x13, x14;

  Multiplier #(.width(32)) multiplier_1 (.a(A), .b(B), .cout(x11));  // open: out, cin
  Adder #(.width(32)) adder_1 (.a(A), .b(B), .out(x0));  // open: cin, cout
  Subtractor #(.width(32)) subtractor_1 (.a(A), .b(B), .out(x12));  // open: bin, bout
  Shifter #(.width(32)) shifter_1 (.in(A), .\dist (B[4:0]), .out(x1));
  assign x4 = A ^ B;  // XOR_Gate xor_1, 32 bits wide
  assign x6 = A | B;  // OR_Gate or_1, 32 bits wide
  assign x7 = A & B;  // AND_Gate and_1, 32 bits wide
  Multiplier #(.mode("twosComplement"), .width(32)) multiplier_2 (.a(A), .b(B), .out(x8), .cout(x9));  // open: cin
  Shifter #(.shift("lr"), .width(32)) shifter_2 (.in(A), .\dist (B[4:0]), .out(x5));
  Shifter #(.shift("ar"), .width(32)) shifter_3 (.in(A), .\dist (B[4:0]), .out(x13));
  Comparator #(.width(32)) comparator_1 (.a(A), .b(B), .lt(comparator_1_lt));  // open: gt, eq
  assign x2 = {{31{1'b0}}, comparator_1_lt};  // Bit_Extender bit_extender_1
  Adder #(.width(32)) adder_2 (.a(A), .b(B), .out(add0));  // open: cin, cout
  Multiplexer #(.select(4), .width(32)) multiplexer_1 (
    .in0(x0), .in1(x1), .in2(x2), .in3(x3), .in4(x4), .in5(x5), .in6(x6), .in7(x7), .in8(x8), .in9(x9),
    .in10(x10), .in11(x11), .in12(x12), .in13(x13), .in14(x14), .in15(B), .out(ALUResult), .sel(ALUSel));

  // Other names for the same wires on the sheet: x15[31:0] = B

  // Notes on the sheet:
  //   INPUTS to your circuit
  //   DON'T CHANGE THE LOCATIONS OF THE INPUTS AND OUTPUTS!
  //   OUTPUT from your circuit
endmodule
