// Logisim project control-logic.circ as structural Verilog: 1 circuit, main circuit control_logic
module control_logic (
  input  [31:0] Instruction,
  input  BrEq,
  input  BrLt,
  output PCSel,
  output RegWEn,
  output [2:0] ImmSel,
  output BrUn,
  output ASel,
  output BSel,
  output [3:0] ALUSel,
  output MemWEn,
  output [1:0] WBSel
);

  wire add, addi, and_8_out, and_9_out, and_10_out, and_11_out, andi, auipc, beq, bge, bgeu, blt, bltu, bne,
       comparator_1_eq, comparator_2_eq, comparator_3_eq, comparator_4_eq, comparator_5_eq, comparator_6_eq,
       comparator_7_eq, comparator_8_eq, comparator_9_eq, comparator_10_eq, comparator_11_eq,
       comparator_12_eq, comparator_13_eq, comparator_14_eq, comparator_15_eq, comparator_16_eq,
       comparator_17_eq, comparator_18_eq, comparator_19_eq, comparator_20_eq, comparator_21_eq,
       comparator_22_eq, comparator_23_eq, comparator_24_eq, comparator_25_eq, comparator_26_eq,
       comparator_27_eq, comparator_28_eq, comparator_29_eq, comparator_30_eq, comparator_31_eq,
       comparator_32_eq, comparator_33_eq, comparator_34_eq, comparator_35_eq, comparator_36_eq,
       comparator_37_eq, comparator_38_eq, comparator_39_eq, comparator_40_eq, comparator_41_eq,
       comparator_42_eq, comparator_43_eq, comparator_44_eq, comparator_45_eq, comparator_46_eq,
       comparator_47_eq, comparator_48_eq, comparator_49_eq, comparator_50_eq, comparator_51_eq,
       comparator_52_eq, comparator_53_eq, comparator_54_eq, comparator_55_eq, comparator_56_eq,
       comparator_57_eq, comparator_58_eq, comparator_59_eq, comparator_60_eq, comparator_61_eq,
       comparator_62_eq, comparator_63_eq, comparator_64_eq, comparator_65_eq, comparator_66_eq,
       comparator_67_eq, comparator_68_eq, comparator_69_eq, comparator_70_eq, comparator_71_eq,
       comparator_72_eq, comparator_73_eq, comparator_74_eq, comparator_75_eq, comparator_76_eq,
       comparator_77_eq, comparator_78_eq, comparator_79_eq, comparator_80_eq, comparator_81_eq,
       comparator_82_eq, comparator_83_eq, comparator_84_eq, is_and, is_or, is_sll, is_sra, is_srl, is_xor,
       jal, jalr, lb, lh, lui, lw, mul, mulh, mulhu, not_1_out, not_2_out, or_1_out, or_2_out, or_3_out, ori,
       sb, sh, slli, slt, slti, srai, srli, sub, sw, xori;
  wire [5:0] ROMIn;
  wire [15:14] rom_1_data;

  ROM #(.addrWidth(6), .dataWidth(16)) rom_1 (
    .addr(ROMIn), .data({rom_1_data, WBSel, MemWEn, ALUSel, BSel, ASel, BrUn, ImmSel, RegWEn}));
  Comparator #(.width(7)) comparator_1 (.a(7'b0010111), .b(Instruction[6:0]), .eq(comparator_1_eq));  // open: gt, lt
  Comparator #(.width(7)) comparator_2 (.a(7'b0110111), .b(Instruction[6:0]), .eq(comparator_2_eq));  // open: gt, lt
  Comparator #(.width(7)) comparator_3 (.a(7'b1101111), .b(Instruction[6:0]), .eq(comparator_3_eq));  // open: gt, lt
  and and_1 (lui, comparator_2_eq, 1'b1);
  and and_2 (jal, comparator_3_eq, 1'b1);
  and and_3 (auipc, comparator_1_eq, 1'b1);
  or or_1 (or_1_out, blt, bltu);
  not not_1 (not_1_out, BrLt);
  Comparator #(.width(7)) comparator_4 (.a(7'b0010011), .b(Instruction[6:0]), .eq(comparator_4_eq));  // open: gt, lt
  Comparator #(.width(3)) comparator_5 (.a(Instruction[14:12]), .b(3'b000), .eq(comparator_5_eq));  // open: gt, lt
  Comparator #(.width(7)) comparator_6 (.a(7'b0010011), .b(Instruction[6:0]), .eq(comparator_6_eq));  // open: gt, lt
  Comparator #(.width(3)) comparator_7 (.a(Instruction[14:12]), .b(3'b111), .eq(comparator_7_eq));  // open: gt, lt
  Comparator #(.width(7)) comparator_8 (.a(7'b0010011), .b(Instruction[6:0]), .eq(comparator_8_eq));  // open: gt, lt
  Comparator #(.width(3)) comparator_9 (.a(Instruction[14:12]), .b(3'b110), .eq(comparator_9_eq));  // open: gt, lt
  Comparator #(.width(7)) comparator_10 (.a(7'b0010011), .b(Instruction[6:0]), .eq(comparator_10_eq));  // open: gt, lt
  Comparator #(.width(3)) comparator_11 (.a(Instruction[14:12]), .b(3'b100), .eq(comparator_11_eq));  // open: gt, lt
  Priority_Encoder #(.select_enc(6)) priority_encoder_1 (
    .in0(add), .in1(mul), .in2(sub), .in3(is_sll), .in4(mulh), .in5(mulhu), .in6(slt), .in7(is_xor),
    .in8(is_srl), .in9(is_sra), .in10(is_or), .in11(is_and), .in12(lb), .in13(lh), .in14(lw), .in15(addi),
    .in16(slli), .in17(slti), .in18(xori), .in19(srli), .in20(srai), .in21(ori), .in22(andi), .in23(sb),
    .in24(sh), .in25(sw), .in26(beq), .in27(bne), .in28(blt), .in29(bge), .in30(bltu), .in31(bgeu),
    .in32(auipc), .in33(lui), .in34(jal), .in35(jalr), .out(ROMIn));  // open: in36, in37, in38, in39, in40, in41, in42, in43, in44, in45, in46, in47, in48, in49, in50, in51, in52, in53, in54, in55, in56, in57, in58, in59, in60, in61, in62, in63, gs, en_out, en_in
  not not_2 (not_2_out, BrEq);
  or or_2 (or_2_out, bge, bgeu);
  or or_3 (or_3_out, not_1_out, BrEq);
  and and_4 (addi, comparator_4_eq, comparator_5_eq);
  and and_5 (andi, comparator_6_eq, comparator_7_eq);
  and and_6 (ori, comparator_8_eq, comparator_9_eq);
  and and_7 (xori, comparator_10_eq, comparator_11_eq);
  Comparator #(.width(7)) comparator_12 (.a(7'b0100011), .b(Instruction[6:0]), .eq(comparator_12_eq));  // open: gt, lt
  Comparator #(.width(3)) comparator_13 (.a(Instruction[14:12]), .b(3'b000), .eq(comparator_13_eq));  // open: gt, lt
  Comparator #(.width(7)) comparator_14 (.a(7'b0100011), .b(Instruction[6:0]), .eq(comparator_14_eq));  // open: gt, lt
  Comparator #(.width(3)) comparator_15 (.a(Instruction[14:12]), .b(3'b001), .eq(comparator_15_eq));  // open: gt, lt
  Comparator #(.width(7)) comparator_16 (.a(7'b0100011), .b(Instruction[6:0]), .eq(comparator_16_eq));  // open: gt, lt
  Comparator #(.width(3)) comparator_17 (.a(Instruction[14:12]), .b(3'b010), .eq(comparator_17_eq));  // open: gt, lt
  and and_8 (and_8_out, bne, not_2_out);
  and and_9 (and_9_out, beq, BrEq);
  and and_10 (and_10_out, or_1_out, BrLt);
  and and_11 (and_11_out, or_2_out, or_3_out);
  and and_12 (sb, comparator_12_eq, comparator_13_eq);
  and and_13 (sh, comparator_14_eq, comparator_15_eq);
  and and_14 (sw, comparator_16_eq, comparator_17_eq);
  Comparator #(.width(7)) comparator_18 (.a(7'b1100111), .b(Instruction[6:0]), .eq(comparator_18_eq));  // open: gt, lt
  Comparator #(.width(3)) comparator_19 (.a(Instruction[14:12]), .b(3'b000), .eq(comparator_19_eq));  // open: gt, lt
  or or_4 (PCSel, jalr, and_8_out, and_9_out, and_10_out, and_11_out, jal);
  Comparator #(.width(7)) comparator_20 (.a(7'b0000011), .b(Instruction[6:0]), .eq(comparator_20_eq));  // open: gt, lt
  Comparator #(.width(3)) comparator_21 (.a(Instruction[14:12]), .b(3'b000), .eq(comparator_21_eq));  // open: gt, lt
  Comparator #(.width(7)) comparator_22 (.a(7'b0000011), .b(Instruction[6:0]), .eq(comparator_22_eq));  // open: gt, lt
  Comparator #(.width(3)) comparator_23 (.a(Instruction[14:12]), .b(3'b001), .eq(comparator_23_eq));  // open: gt, lt
  Comparator #(.width(7)) comparator_24 (.a(7'b0000011), .b(Instruction[6:0]), .eq(comparator_24_eq));  // open: gt, lt
  Comparator #(.width(3)) comparator_25 (.a(Instruction[14:12]), .b(3'b010), .eq(comparator_25_eq));  // open: gt, lt
  and and_15 (lb, comparator_20_eq, comparator_21_eq);
  and and_16 (lh, comparator_22_eq, comparator_23_eq);
  and and_17 (lw, comparator_24_eq, comparator_25_eq);
  and and_18 (jalr, comparator_18_eq, comparator_19_eq);
  Comparator #(.width(7)) comparator_26 (.a(7'b0010011), .b(Instruction[6:0]), .eq(comparator_26_eq));  // open: gt, lt
  Comparator #(.width(3)) comparator_27 (.a(Instruction[14:12]), .b(3'b001), .eq(comparator_27_eq));  // open: gt, lt
  Comparator #(.width(7)) comparator_28 (.a(Instruction[31:25]), .b({7{1'b0}}), .eq(comparator_28_eq));  // open: gt, lt
  Comparator #(.width(7)) comparator_29 (.a(7'b0010011), .b(Instruction[6:0]), .eq(comparator_29_eq));  // open: gt, lt
  Comparator #(.width(3)) comparator_30 (.a(Instruction[14:12]), .b(3'b101), .eq(comparator_30_eq));  // open: gt, lt
  Comparator #(.width(7)) comparator_31 (.a(Instruction[31:25]), .b({7{1'b0}}), .eq(comparator_31_eq));  // open: gt, lt
  Comparator #(.width(7)) comparator_32 (.a(7'b0010011), .b(Instruction[6:0]), .eq(comparator_32_eq));  // open: gt, lt
  Comparator #(.width(3)) comparator_33 (.a(Instruction[14:12]), .b(3'b101), .eq(comparator_33_eq));  // open: gt, lt
  Comparator #(.width(7)) comparator_34 (
    .a(Instruction[31:25]), .b(7'b0100000), .eq(comparator_34_eq));  // open: gt, lt
  Comparator #(.width(7)) comparator_35 (.a(7'b0010011), .b(Instruction[6:0]), .eq(comparator_35_eq));  // open: gt, lt
  Comparator #(.width(3)) comparator_36 (.a(Instruction[14:12]), .b(3'b010), .eq(comparator_36_eq));  // open: gt, lt
  and and_19 (slti, comparator_35_eq, comparator_36_eq);
  Comparator #(.width(7)) comparator_37 (.a(7'b1100011), .b(Instruction[6:0]), .eq(comparator_37_eq));  // open: gt, lt
  Comparator #(.width(3)) comparator_38 (.a(Instruction[14:12]), .b(3'b000), .eq(comparator_38_eq));  // open: gt, lt
  Comparator #(.width(7)) comparator_39 (.a(7'b1100011), .b(Instruction[6:0]), .eq(comparator_39_eq));  // open: gt, lt
  Comparator #(.width(3)) comparator_40 (.a(Instruction[14:12]), .b(3'b101), .eq(comparator_40_eq));  // open: gt, lt
  Comparator #(.width(7)) comparator_41 (.a(7'b1100011), .b(Instruction[6:0]), .eq(comparator_41_eq));  // open: gt, lt
  Comparator #(.width(3)) comparator_42 (.a(Instruction[14:12]), .b(3'b111), .eq(comparator_42_eq));  // open: gt, lt
  and and_20 (slli, comparator_26_eq, comparator_27_eq, comparator_28_eq);
  and and_21 (srli, comparator_29_eq, comparator_30_eq, comparator_31_eq);
  and and_22 (srai, comparator_32_eq, comparator_33_eq, comparator_34_eq);
  and and_23 (beq, comparator_37_eq, comparator_38_eq);
  and and_24 (bge, comparator_39_eq, comparator_40_eq);
  and and_25 (bgeu, comparator_41_eq, comparator_42_eq);
  Comparator #(.width(7)) comparator_43 (.a(7'b1100011), .b(Instruction[6:0]), .eq(comparator_43_eq));  // open: gt, lt
  Comparator #(.width(3)) comparator_44 (.a(Instruction[14:12]), .b(3'b100), .eq(comparator_44_eq));  // open: gt, lt
  Comparator #(.width(7)) comparator_45 (.a(7'b1100011), .b(Instruction[6:0]), .eq(comparator_45_eq));  // open: gt, lt
  Comparator #(.width(3)) comparator_46 (.a(Instruction[14:12]), .b(3'b110), .eq(comparator_46_eq));  // open: gt, lt
  Comparator #(.width(7)) comparator_47 (.a(7'b1100011), .b(Instruction[6:0]), .eq(comparator_47_eq));  // open: gt, lt
  Comparator #(.width(3)) comparator_48 (.a(Instruction[14:12]), .b(3'b001), .eq(comparator_48_eq));  // open: gt, lt
  Comparator #(.width(7)) comparator_49 (.a(7'b0110011), .b(Instruction[6:0]), .eq(comparator_49_eq));  // open: gt, lt
  Comparator #(.width(3)) comparator_50 (.a(Instruction[14:12]), .b(3'b000), .eq(comparator_50_eq));  // open: gt, lt
  Comparator #(.width(7)) comparator_51 (.a(Instruction[31:25]), .b({7{1'b0}}), .eq(comparator_51_eq));  // open: gt, lt
  Comparator #(.width(7)) comparator_52 (.a(7'b0110011), .b(Instruction[6:0]), .eq(comparator_52_eq));  // open: gt, lt
  Comparator #(.width(3)) comparator_53 (.a(Instruction[14:12]), .b(3'b000), .eq(comparator_53_eq));  // open: gt, lt
  Comparator #(.width(7)) comparator_54 (
    .a(Instruction[31:25]), .b(7'b0100000), .eq(comparator_54_eq));  // open: gt, lt
  Comparator #(.width(7)) comparator_55 (.a(7'b0110011), .b(Instruction[6:0]), .eq(comparator_55_eq));  // open: gt, lt
  Comparator #(.width(3)) comparator_56 (.a(Instruction[14:12]), .b(3'b111), .eq(comparator_56_eq));  // open: gt, lt
  Comparator #(.width(7)) comparator_57 (.a(Instruction[31:25]), .b({7{1'b0}}), .eq(comparator_57_eq));  // open: gt, lt
  Comparator #(.width(7)) comparator_58 (.a(7'b0110011), .b(Instruction[6:0]), .eq(comparator_58_eq));  // open: gt, lt
  Comparator #(.width(3)) comparator_59 (.a(Instruction[14:12]), .b(3'b110), .eq(comparator_59_eq));  // open: gt, lt
  Comparator #(.width(7)) comparator_60 (.a(Instruction[31:25]), .b({7{1'b0}}), .eq(comparator_60_eq));  // open: gt, lt
  Comparator #(.width(7)) comparator_61 (.a(7'b0110011), .b(Instruction[6:0]), .eq(comparator_61_eq));  // open: gt, lt
  Comparator #(.width(3)) comparator_62 (.a(Instruction[14:12]), .b(3'b100), .eq(comparator_62_eq));  // open: gt, lt
  Comparator #(.width(7)) comparator_63 (.a(Instruction[31:25]), .b({7{1'b0}}), .eq(comparator_63_eq));  // open: gt, lt
  Comparator #(.width(7)) comparator_64 (.a(7'b0110011), .b(Instruction[6:0]), .eq(comparator_64_eq));  // open: gt, lt
  Comparator #(.width(3)) comparator_65 (.a(Instruction[14:12]), .b(3'b001), .eq(comparator_65_eq));  // open: gt, lt
  Comparator #(.width(7)) comparator_66 (.a(Instruction[31:25]), .b({7{1'b0}}), .eq(comparator_66_eq));  // open: gt, lt
  and and_26 (blt, comparator_43_eq, comparator_44_eq);
  and and_27 (bltu, comparator_45_eq, comparator_46_eq);
  and and_28 (bne, comparator_47_eq, comparator_48_eq);
  and and_29 (add, comparator_49_eq, comparator_50_eq, comparator_51_eq);
  and and_30 (sub, comparator_52_eq, comparator_53_eq, comparator_54_eq);
  and and_31 (is_and, comparator_55_eq, comparator_56_eq, comparator_57_eq);
  and and_32 (is_or, comparator_58_eq, comparator_59_eq, comparator_60_eq);
  and and_33 (is_xor, comparator_61_eq, comparator_62_eq, comparator_63_eq);
  and and_34 (is_sll, comparator_64_eq, comparator_65_eq, comparator_66_eq);
  Comparator #(.width(7)) comparator_67 (.a(7'b0110011), .b(Instruction[6:0]), .eq(comparator_67_eq));  // open: gt, lt
  Comparator #(.width(3)) comparator_68 (.a(Instruction[14:12]), .b(3'b101), .eq(comparator_68_eq));  // open: gt, lt
  Comparator #(.width(7)) comparator_69 (.a(Instruction[31:25]), .b({7{1'b0}}), .eq(comparator_69_eq));  // open: gt, lt
  Comparator #(.width(7)) comparator_70 (.a(7'b0110011), .b(Instruction[6:0]), .eq(comparator_70_eq));  // open: gt, lt
  Comparator #(.width(3)) comparator_71 (.a(Instruction[14:12]), .b(3'b011), .eq(comparator_71_eq));  // open: gt, lt
  Comparator #(.width(7)) comparator_72 (
    .a(Instruction[31:25]), .b(7'b0000001), .eq(comparator_72_eq));  // open: gt, lt
  Comparator #(.width(7)) comparator_73 (.a(7'b0110011), .b(Instruction[6:0]), .eq(comparator_73_eq));  // open: gt, lt
  Comparator #(.width(3)) comparator_74 (.a(Instruction[14:12]), .b(3'b101), .eq(comparator_74_eq));  // open: gt, lt
  Comparator #(.width(7)) comparator_75 (
    .a(Instruction[31:25]), .b(7'b0100000), .eq(comparator_75_eq));  // open: gt, lt
  Comparator #(.width(7)) comparator_76 (.a(7'b0110011), .b(Instruction[6:0]), .eq(comparator_76_eq));  // open: gt, lt
  Comparator #(.width(3)) comparator_77 (.a(Instruction[14:12]), .b(3'b010), .eq(comparator_77_eq));  // open: gt, lt
  Comparator #(.width(7)) comparator_78 (.a(Instruction[31:25]), .b({7{1'b0}}), .eq(comparator_78_eq));  // open: gt, lt
  Comparator #(.width(7)) comparator_79 (.a(7'b0110011), .b(Instruction[6:0]), .eq(comparator_79_eq));  // open: gt, lt
  Comparator #(.width(3)) comparator_80 (.a(Instruction[14:12]), .b(3'b000), .eq(comparator_80_eq));  // open: gt, lt
  Comparator #(.width(7)) comparator_81 (
    .a(Instruction[31:25]), .b(7'b0000001), .eq(comparator_81_eq));  // open: gt, lt
  Comparator #(.width(7)) comparator_82 (.a(7'b0110011), .b(Instruction[6:0]), .eq(comparator_82_eq));  // open: gt, lt
  Comparator #(.width(3)) comparator_83 (.a(Instruction[14:12]), .b(3'b001), .eq(comparator_83_eq));  // open: gt, lt
  Comparator #(.width(7)) comparator_84 (
    .a(Instruction[31:25]), .b(7'b0000001), .eq(comparator_84_eq));  // open: gt, lt
  and and_35 (is_srl, comparator_67_eq, comparator_68_eq, comparator_69_eq);
  and and_36 (mulhu, comparator_70_eq, comparator_71_eq, comparator_72_eq);
  and and_37 (is_sra, comparator_73_eq, comparator_74_eq, comparator_75_eq);
  and and_38 (slt, comparator_76_eq, comparator_77_eq, comparator_78_eq);
  and and_39 (mul, comparator_79_eq, comparator_80_eq, comparator_81_eq);
  and and_40 (mulh, comparator_82_eq, comparator_83_eq, comparator_84_eq);

  // Notes on the sheet:
  //   INPUTS to your circuit
  //   Connect ROM Input here ->
  //   contents of rom_1 (hex, n*v repeats v):
  //   1001 1401 1601 1081 1481 1581 1101 1201 1281 1681 1301 1381 41 41 41 1041 10c1 1141 1241 12c1 16c1
  //   1341 13c1 1842 1842 1842 4*1064 1074 1074 1067 17c7 2069 2041
  //   ROM FOR CONTROL LOGIC
  //   DON'T CHANGE THE LOCATIONS OF THE INPUTS AND OUTPUTS!
  //   This is only if you choose to do the ROM option
  //   CONNECT
  //   WIRE
  //   TO
  //   USE
  //   ROM
  //   OUTPUT from your circuit
  //   Reminder: If using ROM, use combinational logic for PCSel
endmodule
